// Logisim project Project.circ as structural Verilog: 10 circuits, main circuit Project
module Project (
);

  wire and_3_out, and_4_out, cdm_8_mark5_1_p1, cdm_8_mark5_1_p3, clock, Div, mem, Mul1, Mul2, not_1_out,
       not_2_out, rd_wr_prime, rset, Upd;
  wire [2:0] joystick_1_y;
  wire [3:0] scores_1_higher, scores_1_lower, scores_2_higher, scores_2_lower;
  wire [4:0] kinematicfabulouscontroller_1_ballx, kinematicfabulouscontroller_1_bally,
       kinematicfabulouscontroller_1_leftyout, kinematicfabulouscontroller_1_rightyout,
       kinematicfabulouscontroller_1_zero, leftY, RightY, videochip_1_ballx_2, videochip_1_bally_2,
       videochip_1_chipid_2, videochip_1_leftbaty_2, videochip_1_rightbaty_2, videochip_2_ballx_2,
       videochip_2_bally_2, videochip_2_chipid_2, videochip_2_leftbaty_2, videochip_2_rightbaty_2,
       videochip_3_ballx_2, videochip_3_bally_2, videochip_3_chipid_2, videochip_3_leftbaty_2,
       videochip_3_rightbaty_2;
  wire [7:0] addr, and_1_out, and_2_out, cdm_8_mark5_1_p7, cdm_8_mark5_1_p8, CoordY, data, Ls,
       multiplexer_1_out, multiplier_1_cout, multiplier_1_out, other, Reflects, register_1_q, register_2_q,
       register_3_q, Rs, vx, vy, xball, yball;
  wire [15:0] bit_extender_1_out, divider_1_out, divider_2_out, divider_2_rem;
  wire [31:0] videochip_1_column0, videochip_1_column1, videochip_1_column2, videochip_1_column3,
       videochip_1_column4, videochip_1_column5, videochip_1_column6, videochip_1_column7,
       videochip_2_column0, videochip_2_column1, videochip_2_column2, videochip_2_column3,
       videochip_2_column4, videochip_2_column5, videochip_2_column6, videochip_2_column7,
       videochip_3_column0, videochip_3_column1, videochip_3_column2, videochip_3_column3,
       videochip_3_column4, videochip_3_column5, videochip_3_column6, videochip_3_column7,
       videochip_4_column0, videochip_4_column1, videochip_4_column2, videochip_4_column3,
       videochip_4_column4, videochip_4_column5, videochip_4_column6, videochip_4_column7;

  Clock clock_1 (.out(clock));
  // Probe on nothing
  assign and_1_out = addr & 8'hf0;  // AND_Gate and_1, 8 bits wide
  assign and_2_out = addr & 8'hf0;  // AND_Gate and_2, 8 bits wide
  // Probe on data
  // Probe on cdm_8_mark5_1_p3
  // Probe on cdm_8_mark5_1_p1
  // Probe on nothing
  // Probe on nothing
  // Probe on nothing
  Multiplexer #(.select(3), .width(8)) multiplexer_1 (
    .in0(xball), .in1(yball), .in2(vx), .in3(vy), .in4(CoordY), .in5(Reflects), .in6({8{1'b0}}),
    .in7({8{1'b0}}), .out(multiplexer_1_out), .sel(addr[2:0]), .en(and_3_out));
  not not_1 (not_1_out, addr[3]);
  and and_3 (and_3_out, not_1_out, and_1_out[7], and_1_out[6], and_1_out[5], and_1_out[4], mem);
  Decoder #(.select(3), .disabled(0)) decoder_1 (
    .out0(Upd), .out1(Mul1), .out2(Mul2), .out3(Div), .sel(addr[2:0]), .en(and_4_out));  // open: out4, out5, out6, out7
  and and_4 (and_4_out, addr[3], and_2_out[7], and_2_out[6], and_2_out[5], and_2_out[4], mem);
  Register register_1 (.D(data), .en(Mul1), .Q(register_1_q), .clk(clock));  // open: clr
  // Probe on register_1_q
  // Probe on register_2_q
  Register register_2 (.D(data), .en(Mul2), .Q(register_2_q), .clk(clock));  // open: clr
  // Probe on nothing
  // CdM_8_mark5 cdm_8_mark5_1: pin names not known; wires that end beside it: cdm_8_mark5_1_p1, clock, cdm_8_mark5_1_p3, mem, rd_wr_prime, addr, cdm_8_mark5_1_p7, cdm_8_mark5_1_p8
  Multiplexer #(.width(8)) multiplexer_2 (
    .in0(other), .in1(multiplexer_1_out), .out(cdm_8_mark5_1_p8), .sel(and_3_out));  // open: en
  Multiplier multiplier_1 (
    .a(register_1_q), .b(register_2_q), .out(multiplier_1_out), .cout(multiplier_1_cout));  // open: cin
  Register register_3 (.D(data), .en(Div), .Q(register_3_q), .clk(clock));  // open: clr
  assign bit_extender_1_out = {{8{1'b0}}, register_3_q};  // Bit_Extender bit_extender_1
  assign data = not_2_out ? cdm_8_mark5_1_p7 : 8'bz;  // Controlled_Buffer controlled_buffer_1
  not not_2 (not_2_out, rd_wr_prime);
  assign other = rd_wr_prime ? data : 8'bz;  // Controlled_Buffer controlled_buffer_2
  // Probe on bit_extender_1_out
  // Probe on {multiplier_1_cout, multiplier_1_out}
  RAM ram_1 (.addr(addr), .data(data), .sel(mem), .clk(clock), .ld(rd_wr_prime));  // open: clr
  Divider #(.width(16)) divider_1 (
    .a({multiplier_1_cout, multiplier_1_out}), .b(bit_extender_1_out), .out(divider_1_out));  // open: upper, rem
  // Probe on divider_1_out
  Divider #(.width(16)) divider_2 (
    .a(divider_1_out), .b(16'h100), .out(divider_2_out), .rem(divider_2_rem));  // open: upper
  // Probe on divider_2_out
  // Probe on divider_2_rem
  Bit_Extender #(.in_width(16), .out_width(8)) bit_extender_2 (.in(divider_2_out), .out(Reflects));
  Bit_Extender #(.in_width(16), .out_width(8)) bit_extender_3 (.in(divider_2_rem), .out(CoordY));
  Hex_Digit_Display hex_digit_display_1 (.value(scores_1_higher));  // open: dp
  Hex_Digit_Display hex_digit_display_2 (.value(scores_1_lower));  // open: dp
  Scores scores_1 (.Score(Ls), .Higher(scores_1_higher), .Lower(scores_1_lower));
  Joystick #(.bits(3)) joystick_1 (.y(joystick_1_y));  // open: x
  Button R (.out(rset));
  DotMatrix #(.matrixcols(32), .matrixrows(32)) dotmatrix_1 (
    .col0(videochip_1_column0), .col1(videochip_1_column1), .col2(videochip_1_column2),
    .col3(videochip_1_column3), .col4(videochip_1_column4), .col5(videochip_1_column5),
    .col6(videochip_1_column6), .col7(videochip_1_column7), .col8(videochip_2_column0),
    .col9(videochip_2_column1), .col10(videochip_2_column2), .col11(videochip_2_column3),
    .col12(videochip_2_column4), .col13(videochip_2_column5), .col14(videochip_2_column6),
    .col15(videochip_2_column7), .col16(videochip_3_column0), .col17(videochip_3_column1),
    .col18(videochip_3_column2), .col19(videochip_3_column3), .col20(videochip_3_column4),
    .col21(videochip_3_column5), .col22(videochip_3_column6), .col23(videochip_3_column7),
    .col24(videochip_4_column0), .col25(videochip_4_column1), .col26(videochip_4_column2),
    .col27(videochip_4_column3), .col28(videochip_4_column4), .col29(videochip_4_column5),
    .col30(videochip_4_column6), .col31(videochip_4_column7));
  KinematicFabulousController kinematicfabulouscontroller_1 (
    .reset(rset), .leftYin(leftY), .rightYin(RightY), .xball(xball), .yball(yball), .scoreA(Rs), .scoreB(Ls),
    .zero(kinematicfabulouscontroller_1_zero), .ballX(kinematicfabulouscontroller_1_ballx),
    .ballY(kinematicfabulouscontroller_1_bally), .rightYout(kinematicfabulouscontroller_1_rightyout),
    .leftYout(kinematicfabulouscontroller_1_leftyout), .clock(clock), .vxwide(vx), .vywide(vy), .Upd(Upd),
    .Sought(data[7:3]), .leftVYin(joystick_1_y));
  VideoChip videochip_1 (
    .ballX(kinematicfabulouscontroller_1_ballx), .ballY(kinematicfabulouscontroller_1_bally),
    .chipID(kinematicfabulouscontroller_1_zero), .leftbatY(kinematicfabulouscontroller_1_leftyout),
    .rightbatY(kinematicfabulouscontroller_1_rightyout), .ballX_2(videochip_1_ballx_2),
    .ballY_2(videochip_1_bally_2), .chipID_2(videochip_1_chipid_2), .leftbatY_2(videochip_1_leftbaty_2),
    .rightbatY_2(videochip_1_rightbaty_2), .column0(videochip_1_column0), .column1(videochip_1_column1),
    .column2(videochip_1_column2), .column3(videochip_1_column3), .column4(videochip_1_column4),
    .column5(videochip_1_column5), .column6(videochip_1_column6), .column7(videochip_1_column7));
  VideoChip videochip_2 (
    .ballX(videochip_1_ballx_2), .ballY(videochip_1_bally_2), .chipID(videochip_1_chipid_2),
    .leftbatY(videochip_1_leftbaty_2), .rightbatY(videochip_1_rightbaty_2), .ballX_2(videochip_2_ballx_2),
    .ballY_2(videochip_2_bally_2), .chipID_2(videochip_2_chipid_2), .leftbatY_2(videochip_2_leftbaty_2),
    .rightbatY_2(videochip_2_rightbaty_2), .column0(videochip_2_column0), .column1(videochip_2_column1),
    .column2(videochip_2_column2), .column3(videochip_2_column3), .column4(videochip_2_column4),
    .column5(videochip_2_column5), .column6(videochip_2_column6), .column7(videochip_2_column7));
  VideoChip videochip_3 (
    .ballX(videochip_2_ballx_2), .ballY(videochip_2_bally_2), .chipID(videochip_2_chipid_2),
    .leftbatY(videochip_2_leftbaty_2), .rightbatY(videochip_2_rightbaty_2), .ballX_2(videochip_3_ballx_2),
    .ballY_2(videochip_3_bally_2), .chipID_2(videochip_3_chipid_2), .leftbatY_2(videochip_3_leftbaty_2),
    .rightbatY_2(videochip_3_rightbaty_2), .column0(videochip_3_column0), .column1(videochip_3_column1),
    .column2(videochip_3_column2), .column3(videochip_3_column3), .column4(videochip_3_column4),
    .column5(videochip_3_column5), .column6(videochip_3_column6), .column7(videochip_3_column7));
  VideoChip videochip_4 (
    .ballX(videochip_3_ballx_2), .ballY(videochip_3_bally_2), .chipID(videochip_3_chipid_2),
    .leftbatY(videochip_3_leftbaty_2), .rightbatY(videochip_3_rightbaty_2), .leftbatY_2(leftY),
    .rightbatY_2(RightY), .column0(videochip_4_column0), .column1(videochip_4_column1),
    .column2(videochip_4_column2), .column3(videochip_4_column3), .column4(videochip_4_column4),
    .column5(videochip_4_column5), .column6(videochip_4_column6), .column7(videochip_4_column7));  // open: ballX_2, ballY_2, chipID_2
  Hex_Digit_Display hex_digit_display_3 (.value(scores_2_higher));  // open: dp
  Hex_Digit_Display hex_digit_display_4 (.value(scores_2_lower));  // open: dp
  Scores scores_2 (.Score(Rs), .Higher(scores_2_higher), .Lower(scores_2_lower));

  // Other names for the same wires on the sheet: Sought[4:0] = data[7:3]
endmodule

module VideoChip (
  input  [4:0] ballX,
  input  [4:0] ballY,
  input  [4:0] chipID,
  input  [4:0] leftbatY,
  input  [4:0] rightbatY,
  output [31:0] column0,
  output [31:0] column1,
  output [31:0] column2,
  output [31:0] column3,
  output [31:0] column4,
  output [31:0] column5,
  output [31:0] column6,
  output [31:0] column7,
  output [4:0] ballX_2,
  output [4:0] ballY_2,
  output [4:0] chipID_2,
  output [4:0] leftbatY_2,
  output [4:0] rightbatY_2
);

  wire comparator_3_eq, comparator_4_eq, comparator_5_eq, comparator_6_eq, comparator_7_eq, comparator_8_eq,
       comparator_9_eq, comparator_10_eq, isThree, isZero;
  wire [4:0] IDColumn0, IDColumn1, IDColumn2, IDColumn3, IDColumn4, IDColumn5, IDColumn6, IDColumn7;
  wire [31:0] ballColumn, batpixels_1_vertical, batpixels_2_vertical, RAWcolumn3, RAWcolumn4, REScolumn3,
       REScolumn4;

  GetColumnIds getcolumnids_1 (
    .chipID(chipID), .IDColumn0(IDColumn0), .IDColumn1(IDColumn1), .IDColumn2(IDColumn2),
    .IDColumn3(IDColumn3), .IDColumn4(IDColumn4), .IDColumn5(IDColumn5), .IDColumn6(IDColumn6),
    .IDColumn7(IDColumn7));
  Comparator #(.width(5)) comparator_1 (.a(chipID), .b({5{1'b0}}), .eq(isZero));  // open: gt, lt
  BatPixels batpixels_1 (.BatY(leftbatY), .Vertical(batpixels_1_vertical));
  Comparator #(.width(5)) comparator_2 (.a(chipID), .b(5'b00011), .eq(isThree));  // open: gt, lt
  BatPixels batpixels_2 (.BatY(rightbatY), .Vertical(batpixels_2_vertical));
  Shifter #(.width(32)) shifter_1 (.in(32'h1), .\dist (ballY), .out(ballColumn));
  assign REScolumn3 = ballColumn | RAWcolumn3;  // OR_Gate or_1, 32 bits wide
  assign REScolumn4 = ballColumn | RAWcolumn4;  // OR_Gate or_2, 32 bits wide
  Multiplexer #(.width(32)) multiplexer_1 (
    .in0({32{1'b0}}), .in1(batpixels_1_vertical), .out(RAWcolumn3), .sel(isZero));  // open: en
  Multiplexer #(.width(32)) multiplexer_2 (
    .in0({32{1'b0}}), .in1(batpixels_2_vertical), .out(RAWcolumn4), .sel(isThree));  // open: en
  Multiplexer #(.width(32)) multiplexer_3 (
    .in0({32{1'b0}}), .in1(ballColumn), .out(column0), .sel(comparator_3_eq));  // open: en
  Comparator #(.width(5)) comparator_3 (.a(IDColumn0), .b(ballX), .eq(comparator_3_eq));  // open: gt, lt
  Multiplexer #(.width(32)) multiplexer_4 (
    .in0(RAWcolumn3), .in1(REScolumn3), .out(column3), .sel(comparator_4_eq));  // open: en
  Comparator #(.width(5)) comparator_4 (.a(IDColumn3), .b(ballX), .eq(comparator_4_eq));  // open: gt, lt
  Multiplexer #(.width(32)) multiplexer_5 (
    .in0({32{1'b0}}), .in1(ballColumn), .out(column1), .sel(comparator_5_eq));  // open: en
  Comparator #(.width(5)) comparator_5 (.a(IDColumn1), .b(ballX), .eq(comparator_5_eq));  // open: gt, lt
  Multiplexer #(.width(32)) multiplexer_6 (
    .in0({32{1'b0}}), .in1(ballColumn), .out(column2), .sel(comparator_6_eq));  // open: en
  Comparator #(.width(5)) comparator_6 (.a(IDColumn2), .b(ballX), .eq(comparator_6_eq));  // open: gt, lt
  Multiplexer #(.width(32)) multiplexer_7 (
    .in0({32{1'b0}}), .in1(ballColumn), .out(column5), .sel(comparator_7_eq));  // open: en
  Comparator #(.width(5)) comparator_7 (.a(IDColumn5), .b(ballX), .eq(comparator_7_eq));  // open: gt, lt
  Multiplexer #(.width(32)) multiplexer_8 (
    .in0({32{1'b0}}), .in1(ballColumn), .out(column6), .sel(comparator_8_eq));  // open: en
  Comparator #(.width(5)) comparator_8 (.a(IDColumn6), .b(ballX), .eq(comparator_8_eq));  // open: gt, lt
  Multiplexer #(.width(32)) multiplexer_9 (
    .in0(RAWcolumn4), .in1(REScolumn4), .out(column4), .sel(comparator_9_eq));  // open: en
  Comparator #(.width(5)) comparator_9 (.a(IDColumn4), .b(ballX), .eq(comparator_9_eq));  // open: gt, lt
  Multiplexer #(.width(32)) multiplexer_10 (
    .in0({32{1'b0}}), .in1(ballColumn), .out(column7), .sel(comparator_10_eq));  // open: en
  Comparator #(.width(5)) comparator_10 (.a(IDColumn7), .b(ballX), .eq(comparator_10_eq));  // open: gt, lt
  Adder #(.width(5)) adder_1 (.a(chipID), .b({5{1'b0}}), .out(chipID_2), .cin(1'b1));  // open: cout

  assign ballX_2 = ballX;
  assign ballY_2 = ballY;
  assign leftbatY_2 = leftbatY;
  assign rightbatY_2 = rightbatY;

  // Other names for the same wires on the sheet: FINALcolumn0[31:0] = column0; FINALcolumn1[31:0] = column1;
  //   FINALcolumn2[31:0] = column2; FINALcolumn3[31:0] = column3; FINALcolumn4[31:0] = column4;
  //   FINALcolumn5[31:0] = column5; FINALcolumn6[31:0] = column6; FINALcolumn7[31:0] = column7

  // Notes on the sheet:
  //   INPUTS
  //   CHECK IF ==0
  //   CHECK IF ==3
  //   GET RES 3
  //   GET ADDRESSES
  //   GET RAW 3
  //   GET RAW 4
  //   GET RAW != 3 && != 4
  //   GET RES 4
  //   SELECT W OR W/O BALL IN THE COLUMN
  //   PASS THE COORDINATES
  //   LOAD RESULTS
endmodule

module GetColumnIds (
  input  [4:0] chipID,
  output [4:0] IDColumn0,
  output [4:0] IDColumn1,
  output [4:0] IDColumn2,
  output [4:0] IDColumn3,
  output [4:0] IDColumn4,
  output [4:0] IDColumn5,
  output [4:0] IDColumn6,
  output [4:0] IDColumn7
);

  wire [4:0] resID;

  Multiplier #(.width(5)) multiplier_1 (.a(chipID), .b(5'b01000), .out(resID));  // open: cin, cout
  Adder #(.width(5)) adder_1 (.a(resID), .b({5{1'b0}}), .out(IDColumn0));  // open: cin, cout
  Adder #(.width(5)) adder_2 (.a(resID), .b(5'b00001), .out(IDColumn1));  // open: cin, cout
  Adder #(.width(5)) adder_3 (.a(resID), .b(5'b00010), .out(IDColumn2));  // open: cin, cout
  Adder #(.width(5)) adder_4 (.a(resID), .b(5'b00011), .out(IDColumn3));  // open: cin, cout
  Adder #(.width(5)) adder_5 (.a(resID), .b(5'b00100), .out(IDColumn4));  // open: cin, cout
  Adder #(.width(5)) adder_6 (.a(resID), .b(5'b00101), .out(IDColumn5));  // open: cin, cout
  Adder #(.width(5)) adder_7 (.a(resID), .b(5'b00110), .out(IDColumn6));  // open: cin, cout
  Adder #(.width(5)) adder_8 (.a(resID), .b(5'b00111), .out(IDColumn7));  // open: cin, cout

  // Notes on the sheet:
  //   INPUTS
  //   GET ZEROE'S ADDRESS
  //   COUNT ALL ADDRESSES
endmodule

module KinematicFabulousController (
  input  clock,
  input  reset,
  input  [4:0] leftYin,
  input  Upd,
  input  [4:0] rightYin,
  input  [4:0] Sought,
  input  [2:0] leftVYin,
  output [7:0] xball,
  output [7:0] yball,
  output [7:0] vxwide,
  output [7:0] vywide,
  output [7:0] scoreA,
  output [7:0] scoreB,
  output [4:0] zero,
  output [4:0] ballX,
  output [4:0] ballY,
  output [4:0] rightYout,
  output [4:0] leftYout
);

  wire adder_2_cout, adder_3_cout, adder_6_cout, adder_8_cout, and_1_out, and_4_out, and_6_out, Bcontact,
       bigtan, comparator_1_lt, comparator_2_gt, comparator_3_gt, comparator_4_lt, comparator_5_eq,
       comparator_6_eq, comparator_7_gt, enRYREG, enSCA, enSCB, enVX, enVY, enXREG, enYREG, hitA, hitB,
       inrange_1_hit, inrange_2_hit, LBcontact, nor_1_out, not_1_out, not_2_out, not_3_out, or_2_out,
       RBcontact, xor_3_out, xor_4_out, xor_5_out, xrefl, yrefl;
  wire [2:0] adder_1_out, counter_1_q, negator_1_out;
  wire [4:0] bit_extender_4_out, counter_2_q, increment_1_goal, increment_1_result, leftVYin_t,
       multiplexer_1_out, multiplexer_3_out, multiplexer_4_out, rightYin_t, tmpSum, uplRYREG;
  wire [7:0] adder_11_out, adder_12_out, inrange_1_coord, inrange_2_coord, multiplexer_2_out, uplSCA, uplSCB,
       xreg, yreg;
  wire [11:0] divider_1_out, multiplexer_5_out, multiplexer_6_out, multiplexer_7_out, multiplexer_8_out,
       multiplexer_16_out, multiplexer_17_out, multiply_1_result, multiply_2_result, multiply_3_result,
       multiply_4_result, negator_2_out, negator_3_out, negator_4_out, negator_5_out, rom_1_data, rom_2_data,
       uplVX, uplVY, vx, vxlimit, vxnew, vxrefl, vy, vylimit, vynew, vyrefl;
  wire [15:0] adder_4_out, adder_7_out, adder_9_out, adder_10_out, longVX, longVY, uplXREG, uplYREG;

  Register #(.width(16), .trigger("falling")) u_xreg (
    .D(uplXREG), .en(enXREG), .Q({ballX, xball[2:0], xreg}), .clk(clock));  // open: clr
  Register #(.width(16), .trigger("falling")) u_yreg (
    .D(uplYREG), .en(enYREG), .Q({ballY, yball[2:0], yreg}), .clk(clock));  // open: clr
  Register #(.width(12)) u_vx (.D(uplVX), .en(enVX), .Q({vx[11:9], vxwide, vx[0]}), .clk(clock));  // open: clr
  Register #(.width(12)) u_vy (.D(uplVY), .en(enVY), .Q({vy[11:9], vywide, vy[0]}), .clk(clock));  // open: clr
  Negator #(.width(3)) negator_1 (.in(adder_1_out), .out(negator_1_out));
  Adder #(.width(3)) adder_1 (.a(leftVYin), .b(3'b100), .out(adder_1_out));  // open: cin, cout
  Register scA (.D(uplSCA), .en(enSCA), .Q(scoreA), .clk(clock));  // open: clr
  Register scB (.D(uplSCB), .en(enSCB), .Q(scoreB), .clk(clock));  // open: clr
  Register #(.width(5), .trigger("falling")) rightYreg (
    .D(uplRYREG), .en(enRYREG), .Q(rightYout), .clk(clock));  // open: clr
  assign longVX = {{4{vx[11]}}, {vx[11:9], vxwide, vx[0]}};  // Bit_Extender bit_extender_1
  assign longVY = {{4{vy[11]}}, {vy[11:9], vywide, vy[0]}};  // Bit_Extender bit_extender_2
  Adder #(.width(16)) adder_2 (.a(longVX), .b({ballX, xball[2:0], xreg}), .cout(adder_2_cout));  // open: out, cin
  xor xor_1 (xrefl, adder_2_cout, longVX[15]);
  Adder #(.width(16)) adder_3 (.a(longVY), .b({ballY, yball[2:0], yreg}), .cout(adder_3_cout));  // open: out, cin
  xor xor_2 (yrefl, adder_3_cout, longVY[15]);
  assign leftVYin_t = {{2{negator_1_out[2]}}, negator_1_out};  // Bit_Extender bit_extender_3
  Comparator #(.width(5), .mode("unsigned")) comparator_1 (
    .a(tmpSum), .b(leftYin), .lt(comparator_1_lt));  // open: gt, eq
  Comparator #(.width(5)) comparator_2 (.a(leftVYin_t), .b({5{1'b0}}), .gt(comparator_2_gt));  // open: eq, lt
  not not_1 (not_1_out, longVX[15]);
  and and_1 (and_1_out, comparator_1_lt, comparator_2_gt);
  and and_2 (hitA, xrefl, longVX[15]);
  and and_3 (hitB, xrefl, not_1_out);
  Adder #(.width(16)) adder_4 (.a({ballX, xball[2:0], xreg}), .b(16'he200), .out(adder_4_out));  // open: cin, cout
  Adder #(.width(5)) adder_5 (.a(leftVYin_t), .b(leftYin), .out(tmpSum));  // open: cin, cout
  Comparator #(.width(5), .mode("unsigned")) comparator_3 (
    .a(tmpSum), .b(leftYin), .gt(comparator_3_gt));  // open: eq, lt
  Comparator #(.width(5)) comparator_4 (.a(leftVYin_t), .b({5{1'b0}}), .lt(comparator_4_lt));  // open: gt, eq
  Adder #(.width(16)) adder_6 (.a(adder_4_out), .b(longVX), .cout(adder_6_cout));  // open: out, cin
  xor xor_3 (xor_3_out, adder_6_cout, longVX[15]);
  Inrange inrange_1 (
    .hit(inrange_1_hit), .Coord(inrange_1_coord), .Yball({ballY, yball[2:0]}), .Ybat({leftYout, 3'b000}));
  or or_1 (Bcontact, LBcontact, RBcontact);
  Increment increment_1 (
    .Clock(clock), .Sought(Sought), .Cur(rightYin), .result(increment_1_result), .Update(Upd),
    .goal(increment_1_goal));
  // Probe on increment_1_goal
  Multiplexer #(.width(5), .enable("false")) multiplexer_1 (
    .in0(tmpSum), .in1({5{1'b1}}), .out(multiplexer_1_out), .sel(and_1_out));
  and and_4 (and_4_out, comparator_3_gt, comparator_4_lt);
  and and_5 (LBcontact, xor_3_out, inrange_1_hit);
  // Probe on multiplexer_2_out
  Bit_Extender #(.out_width(5)) bit_extender_4 (.in(multiplexer_2_out), .out(bit_extender_4_out));
  Multiplexer #(.width(8)) multiplexer_2 (
    .in0(inrange_2_coord), .in1(inrange_1_coord), .out(multiplexer_2_out), .sel(LBcontact), .en(Bcontact));
  Register #(.width(5)) register_1 (.D(increment_1_result), .Q(rightYin_t), .clk(comparator_5_eq));  // open: en, clr
  Multiplexer #(.width(5), .enable("false")) multiplexer_3 (
    .in0(multiplexer_1_out), .in1({5{1'b0}}), .out(multiplexer_3_out), .sel(and_4_out));
  Multiplexer #(.width(5), .enable("false")) multiplexer_4 (
    .in0(multiplexer_3_out), .in1(5'b01111), .out(multiplexer_4_out), .sel(reset));
  and and_6 (and_6_out, reset, ~clock);  // AND_Gate
  Adder #(.width(16)) adder_7 (.a({ballX, xball[2:0], xreg}), .b(16'h1e00), .out(adder_7_out));  // open: cin, cout
  Adder #(.width(16)) adder_8 (.a(adder_7_out), .b(longVX), .cout(adder_8_cout));  // open: out, cin
  xor xor_4 (xor_4_out, adder_8_cout, longVX[15]);
  Inrange inrange_2 (
    .hit(inrange_2_hit), .Coord(inrange_2_coord), .Yball({ballY, yball[2:0]}), .Ybat({rightYout, 3'b000}));
  Counter #(.width(3), .max('h3)) counter_1 (.load(1'b1), .Q(counter_1_q), .clk(clock));  // open: D, count, carry, clr
  Register #(.width(5)) register_2 (.D(multiplexer_4_out), .Q(leftYout), .clk(or_2_out));  // open: en, clr
  or or_2 (or_2_out, and_6_out, comparator_6_eq);
  Counter #(.width(5), .max('h9)) counter_2 (.Q(counter_2_q), .clk(clock));  // open: load, D, count, carry, clr
  and and_7 (RBcontact, xor_4_out, inrange_2_hit);
  ROM #(.addrWidth(5), .dataWidth(12)) rom_1 (.addr(bit_extender_4_out), .data(rom_1_data), .sel(Bcontact));
  ROM #(.addrWidth(5), .dataWidth(12)) rom_2 (.addr(bit_extender_4_out), .data(rom_2_data), .sel(Bcontact));
  Comparator #(.width(3)) comparator_5 (.a(counter_1_q), .b(3'b001), .eq(comparator_5_eq));  // open: gt, lt
  Comparator #(.width(5)) comparator_6 (.a(counter_2_q), .b(5'b01001), .eq(comparator_6_eq));  // open: gt, lt
  xor xor_5 (xor_5_out, rom_1_data[11], RBcontact);
  // Probe on vxrefl
  // Probe on vyrefl
  Multiply multiply_1 (
    .velocity(vxrefl), .sincos(rom_1_data[10:0]), .Result(multiply_1_result), .sincos_sign(xor_5_out));
  Multiply multiply_2 (
    .velocity(vyrefl), .sincos(rom_2_data[10:0]), .Result(multiply_2_result), .sincos_sign(rom_2_data[11]));
  Subtractor #(.width(12)) subtractor_1 (.a(multiply_1_result), .b(multiply_2_result), .out(vynew));  // open: bin, bout
  // Probe on {vy[11:9], vywide, vy[0]}
  Multiplexer #(.width(12)) multiplexer_5 (
    .in0(vxrefl), .in1(vxlimit), .out(multiplexer_5_out), .sel(bigtan));  // open: en
  Multiplexer #(.width(12)) multiplexer_6 (
    .in0(vyrefl), .in1(vylimit), .out(multiplexer_6_out), .sel(bigtan));  // open: en
  // Probe on vynew
  Adder #(.width(16)) adder_9 (.a({ballX, xball[2:0], xreg}), .b(longVX), .out(adder_9_out));  // open: cin, cout
  Adder #(.width(16)) adder_10 (.a({ballY, yball[2:0], yreg}), .b(longVY), .out(adder_10_out));  // open: cin, cout
  Multiplexer #(.width(12)) multiplexer_7 (
    .in0(multiplexer_5_out), .in1(vxnew), .out(multiplexer_7_out), .sel(Bcontact));  // open: en
  Multiplexer #(.width(12)) multiplexer_8 (
    .in0(multiplexer_6_out), .in1(vynew), .out(multiplexer_8_out), .sel(Bcontact));  // open: en
  Adder adder_11 (.a(scoreA), .b(8'h1), .out(adder_11_out));  // open: cin, cout
  Adder adder_12 (.a(scoreB), .b(8'h1), .out(adder_12_out));  // open: cin, cout
  Multiply multiply_3 (
    .velocity(vyrefl), .sincos(rom_1_data[10:0]), .Result(multiply_3_result), .sincos_sign(xor_5_out));
  Multiply multiply_4 (
    .velocity(vxrefl), .sincos(rom_2_data[10:0]), .Result(multiply_4_result), .sincos_sign(rom_2_data[11]));
  Multiplexer #(.width(16)) multiplexer_9 (.in0(adder_9_out), .in1(16'hc000), .out(uplXREG), .sel(reset));  // open: en
  Multiplexer #(.width(16)) multiplexer_10 (
    .in0(adder_10_out), .in1(16'h7800), .out(uplYREG), .sel(reset));  // open: en
  Multiplexer #(.width(5)) multiplexer_11 (.in0(rightYin_t), .in1(5'b01111), .out(uplRYREG), .sel(reset));  // open: en
  Multiplexer #(.width(12)) multiplexer_12 (
    .in0(multiplexer_7_out), .in1(12'hf90), .out(uplVX), .sel(reset));  // open: en
  Multiplexer #(.width(12)) multiplexer_13 (
    .in0(multiplexer_8_out), .in1(12'h3e), .out(uplVY), .sel(reset));  // open: en
  Multiplexer #(.width(8)) multiplexer_14 (.in0(adder_11_out), .in1({8{1'b0}}), .out(uplSCA), .sel(reset));  // open: en
  Multiplexer #(.width(8)) multiplexer_15 (.in0(adder_12_out), .in1({8{1'b0}}), .out(uplSCB), .sel(reset));  // open: en
  Adder #(.width(12)) adder_13 (.a(multiply_3_result), .b(multiply_4_result), .out(vxnew));  // open: cin, cout
  // Probe on vxnew
  // Probe on {vx[11:9], vxwide, vx[0]}
  nor nor_1 (nor_1_out, xrefl, Bcontact);
  not not_2 (not_2_out, yrefl);
  not not_3 (not_3_out, ballX[4]);
  or or_3 (enXREG, nor_1_out, reset);
  or or_4 (enYREG, not_2_out, reset);
  or or_5 (enRYREG, not_3_out, reset);
  or or_6 (enVX, xrefl, Bcontact, reset, bigtan);
  or or_7 (enVY, yrefl, Bcontact, reset, bigtan);
  or or_8 (enSCA, hitA, reset);
  or or_9 (enSCB, hitB, reset);
  Multiplexer #(.width(12)) multiplexer_16 (
    .in0({vy[11:9], vywide, vy[0]}), .in1(negator_2_out), .out(multiplexer_16_out), .sel(vy[11]));  // open: en
  Negator #(.width(12)) negator_2 (.in({vy[11:9], vywide, vy[0]}), .out(negator_2_out));
  Multiplexer #(.width(12)) multiplexer_17 (
    .in0({vx[11:9], vxwide, vx[0]}), .in1(negator_3_out), .out(multiplexer_17_out), .sel(vx[11]));  // open: en
  Negator #(.width(12)) negator_3 (.in({vx[11:9], vxwide, vx[0]}), .out(negator_3_out));
  Divider #(.width(12)) divider_1 (
    .a(multiplexer_16_out), .b(multiplexer_17_out), .out(divider_1_out));  // open: upper, rem
  Reflect reflect_1 (.oldv({vx[11:9], vxwide, vx[0]}), .newv(vxrefl));
  Reflect reflect_2 (.oldv({vy[11:9], vywide, vy[0]}), .newv(vyrefl));
  Multiplexer #(.width(12)) multiplexer_18 (
    .in0(12'h1f), .in1(negator_4_out), .out(vxlimit), .sel(vx[11]));  // open: en
  Negator #(.width(12)) negator_4 (.in(12'h1f), .out(negator_4_out));
  Multiplexer #(.width(12)) multiplexer_19 (
    .in0(12'h7c), .in1(negator_5_out), .out(vylimit), .sel(vy[11]));  // open: en
  Negator #(.width(12)) negator_5 (.in(12'h7c), .out(negator_5_out));
  Comparator #(.width(12), .mode("unsigned")) comparator_7 (
    .a(divider_1_out), .b(12'h3), .gt(comparator_7_gt));  // open: eq, lt
  and and_8 (bigtan, comparator_7_gt, ~reset, ~xrefl, ~yrefl, ~Bcontact);  // AND_Gate

  assign xball[7:3] = ballX;
  assign yball[7:3] = ballY;
  assign zero = {5{1'b0}};

  // Other names for the same wires on the sheet: leftY_8[7:3] = leftYout; leftYin_t[4:0] = leftYout;
  //   vxneg = longVX[15]; vyneg = longVY[15]; rightY_8[7:3] = rightYout; rightYreg[4:0] = rightYout;
  //   scA[7:0] = scoreA; scB[7:0] = scoreB; tempLeft[4:0] = leftYin; tempRight[4:0] = rightYin; vx[8:1] = vxwide;
  //   vx_8[7:0] = vxwide; vy[8:1] = vywide; vy_8[7:0] = vywide; xreg[15:8] = {ballX, xball[2:0]};
  //   xreg_8[7:0] = {ballX, xball[2:0]}; yreg[15:8] = {ballY, yball[2:0]}; yreg_8[7:0] = {ballY, yball[2:0]}

  // Notes on the sheet:
  //   LATCHES
  //   INPUTS
  //   COMBINATIONAL
  //   INCREASING BAT's Ys
  //   contents of rom_1 (hex, n*v repeats v):
  //   5cf 572 50c 49f 429 3ac 329 29f 20f 17c e5 4d 84d 8e5 97c a0f a9f b29 bac c29 c9f d0c d72 dcf
  //   contents of rom_2 (hex, n*v repeats v):
  //   57f 5db 633 687 6d4 71a 759 78e 7ba 7db 7f2 7fe 7fe 7f2 7db 7ba 78e 759 71a 6d4 687 633 5db 57f
  //   REFLECT BY BAT
  //   BEHAVIOUR
  //   OUTPUTS
endmodule

module Inrange (
  input  [7:0] Yball,
  input  [7:0] Ybat,
  output [7:0] Coord,
  output hit
);

  wire and_1_out, and_2_out, comparator_1_gt, comparator_2_lt, comparator_3_gt, comparator_4_lt,
       comparator_5_lt, nor_1_out;
  wire [7:0] subtractor_1_out;

  Subtractor subtractor_1 (.a(Ybat), .b(8'h8), .out(subtractor_1_out));  // open: bin, bout
  Comparator #(.mode("unsigned")) comparator_1 (.a(Ybat), .b(8'he0), .gt(comparator_1_gt));  // open: eq, lt
  Comparator #(.mode("unsigned")) comparator_2 (.a(Yball), .b(8'h20), .lt(comparator_2_lt));  // open: gt, eq
  Comparator #(.mode("unsigned")) comparator_3 (.a(Ybat), .b(8'he0), .gt(comparator_3_gt));  // open: eq, lt
  Comparator #(.mode("unsigned")) comparator_4 (.a(Yball), .b(8'h20), .lt(comparator_4_lt));  // open: gt, eq
  Subtractor subtractor_2 (.a(Yball), .b(subtractor_1_out), .out(Coord));  // open: bin, bout
  and and_1 (and_1_out, comparator_1_gt, comparator_2_lt);
  nor nor_1 (nor_1_out, and_1_out, and_2_out);
  and and_2 (and_2_out, comparator_3_gt, comparator_4_lt);
  Comparator #(.mode("unsigned")) comparator_5 (.a(Coord), .b(8'h18), .lt(comparator_5_lt));  // open: gt, eq
  and and_3 (hit, comparator_5_lt, nor_1_out);
endmodule

module Reflect (
  input  [11:0] oldv,
  output [11:0] newv
);

  wire comparator_1_eq;
  wire [11:0] adder_1_out, not_1_out;

  Adder #(.width(12)) adder_1 (.a(12'h1), .b(not_1_out), .out(adder_1_out));  // open: cin, cout
  assign not_1_out = ~oldv;  // NOT_Gate not_1, 12 bits wide
  Comparator #(.width(12)) comparator_1 (.a(oldv), .b(12'h800), .eq(comparator_1_eq));  // open: gt, lt
  Multiplexer #(.width(12)) multiplexer_1 (
    .in0(adder_1_out), .in1(not_1_out), .out(newv), .sel(comparator_1_eq));  // open: en
endmodule

module Scores (
  input  [7:0] Score,
  output [3:0] Higher,
  output [3:0] Lower
);

  wire [3:0] bit_extender_1_out;
  wire [7:0] divider_1_out, divider_1_rem;

  Divider divider_1 (.a(Score), .b(8'ha), .out(divider_1_out), .rem(divider_1_rem));  // open: upper
  Bit_Extender #(.out_width(4)) bit_extender_1 (.in(divider_1_out), .out(bit_extender_1_out));
  Bit_Extender #(.out_width(4)) bit_extender_2 (.in(divider_1_rem), .out(Lower));
  Divider #(.width(4)) divider_2 (.a(bit_extender_1_out), .b(4'b1010), .rem(Higher));  // open: out, upper
endmodule

module Increment (
  input  Clock,
  input  [4:0] Sought,
  input  [4:0] Cur,
  input  Update,
  output [4:0] result,
  output [4:0] goal
);

  wire comparator_1_eq, comparator_1_gt;
  wire [4:0] adder_1_out, adder_2_out, multiplexer_1_out;

  Register #(.width(5)) register_1 (.D(Sought), .en(Update), .Q(goal), .clk(Clock));  // open: clr
  Adder #(.width(5)) adder_1 (.a(Cur), .b({5{1'b1}}), .out(adder_1_out));  // open: cin, cout
  Adder #(.width(5)) adder_2 (.a(Cur), .b(5'b00001), .out(adder_2_out));  // open: cin, cout
  Multiplexer #(.width(5)) multiplexer_1 (
    .in0(adder_1_out), .in1(adder_2_out), .out(multiplexer_1_out), .sel(comparator_1_gt));  // open: en
  Comparator #(.width(5), .mode("unsigned")) comparator_1 (
    .a(goal), .b(Cur), .gt(comparator_1_gt), .eq(comparator_1_eq));  // open: lt
  Multiplexer #(.width(5)) multiplexer_2 (
    .in0(multiplexer_1_out), .in1(Cur), .out(result), .sel(comparator_1_eq));  // open: en

  // Other names for the same wires on the sheet: upd = Update
endmodule

module BatPixels (
  input  [4:0] BatY,
  output [31:0] Vertical
);

  wire [4:0] subtractor_1_out;
  wire [31:0] shifter_1_out, shifter_2_out;

  Subtractor #(.width(5)) subtractor_1 (.a({5{1'b1}}), .b(BatY), .out(subtractor_1_out));  // open: bin, bout
  Shifter #(.width(32)) shifter_1 (.in(32'h3), .\dist (BatY), .out(shifter_1_out));
  Shifter #(.width(32), .shift("lr")) shifter_2 (.in(32'h40000000), .\dist (subtractor_1_out), .out(shifter_2_out));
  assign Vertical = shifter_1_out | shifter_2_out;  // OR_Gate or_1, 32 bits wide
endmodule

module Multiply (
  input  [11:0] velocity,
  input  [10:0] sincos,
  input  sincos_sign,
  output [11:0] Result
);

  wire xor_1_out;
  wire [10:0] bit_extender_1_out, multiplier_1_cout, multiplier_1_out;
  wire [11:0] bit_extender_2_out, multiplexer_1_out, negator_1_out, reflect_1_newv;
  wire [21:0] divider_1_out;

  Reflect reflect_1 (.oldv(velocity), .newv(reflect_1_newv));
  Bit_Extender #(.in_width(12), .out_width(11), .\type ("sign")) bit_extender_1 (
    .in(multiplexer_1_out), .out(bit_extender_1_out));
  Multiplexer #(.width(12)) multiplexer_1 (
    .in0(velocity), .in1(reflect_1_newv), .out(multiplexer_1_out), .sel(velocity[11]));  // open: en
  Multiplier #(.width(11)) multiplier_1 (
    .a(bit_extender_1_out), .b(sincos), .out(multiplier_1_out), .cin(11'h3ff), .cout(multiplier_1_cout));
  Divider #(.width(22)) divider_1 (
    .a({multiplier_1_cout, multiplier_1_out}), .b(22'h7ff), .out(divider_1_out));  // open: upper, rem
  Bit_Extender #(.in_width(22), .out_width(12)) bit_extender_2 (.in(divider_1_out), .out(bit_extender_2_out));
  xor xor_1 (xor_1_out, velocity[11], sincos_sign);
  Multiplexer #(.width(12)) multiplexer_2 (
    .in0(bit_extender_2_out), .in1(negator_1_out), .out(Result), .sel(xor_1_out));  // open: en
  Negator #(.width(12)) negator_1 (.in(bit_extender_2_out), .out(negator_1_out));

  // Notes on the sheet:
  //   Velocity is a signed integer number
  //   sincos is a number from 0 to 1
endmodule
